// Logisim project nand2tetris.circ as structural Verilog: 5 circuits, main circuit main
module main (
  input  in_1,
  input  in_2,
  input  in_3,
  input  in_4,
  input  in_5,
  input  in_6,
  input  in_7,
  output out_8,
  output out_9,
  output out_10,
  output out_11
);

  AndGate andgate_1 (.a(in_2), .b(in_3), .outp(out_9));
  NotGate notgate_1 (.inp(in_1), .outp(out_8));
  OrGate orgate_1 (.a(in_5), .b(in_4), .outp(out_10));
  XorGate xorgate_1 (.in_1(in_7), .in_2(in_6), .out_3(out_11));
endmodule

module NotGate (
  input  inp,
  output outp
);

  nand nand_1 (outp, inp, inp);
endmodule

module AndGate (
  input  a,
  input  b,
  output outp
);

  wire nand_1_out;

  nand nand_1 (nand_1_out, a, b);
  NotGate notgate_1 (.inp(nand_1_out), .outp(outp));
endmodule

module OrGate (
  input  a,
  input  b,
  output outp
);

  wire notgate_1_outp, notgate_2_outp;

  NotGate notgate_1 (.inp(a), .outp(notgate_1_outp));
  NotGate notgate_2 (.inp(b), .outp(notgate_2_outp));
  nand nand_1 (outp, notgate_1_outp, notgate_2_outp);
endmodule

module XorGate (
  input  in_1,
  input  in_2,
  output out_3
);

  wire nand_1_out, orgate_1_outp;

  nand nand_1 (nand_1_out, in_1, in_2);
  OrGate orgate_1 (.a(in_2), .b(in_1), .outp(orgate_1_outp));
  AndGate andgate_1 (.a(nand_1_out), .b(orgate_1_outp), .outp(out_3));
endmodule
